// Logisim project APUPlayer.circ as structural Verilog: 6 circuits, main circuit AUXDumper
module APUPlayer (
  input  nRES,
  input  nIRQ
);

  wire apu_m2__ext, apu_nirq_cpu, apu_nnmi_cpu, apu_phi0__cpu, apu_r_w__ext, apu_rdy__cpu, core_phi1,
       core_phi2, core_r_w, XTAL_out;
  wire [7:0] apu_aux_a, apu_data_to_cpu, apu_db_out, core_db_out, wram_db_out;
  wire [14:0] apu_aux_b;
  wire [15:0] apu_ab, core_addr;
  wire [23:0] dumper_addr;
  wire [31:0] dumper_data;

  Clock XTAL (.out(XTAL_out));
  _2A03_APU apu (
    .nRES_PIN(nRES), .RDY__CPU(apu_rdy__cpu), .R_W__CPU(core_r_w), .nIRQ_CPU(apu_nirq_cpu),
    .nNMI_CPU(apu_nnmi_cpu), .nNMI_PIN(1'b1), .R_W__EXT(apu_r_w__ext), .DBG__EXT(1'b0),
    .M2__EXT(apu_m2__ext), .PHI0__CPU(apu_phi0__cpu), .nIRQ_PIN(nIRQ), .Data_to_CPU(apu_data_to_cpu),
    .Data_from_CPU(core_db_out), .AUX_A(apu_aux_a), .AUX_B(apu_aux_b), .CPU_Ax(core_addr), .AB(apu_ab),
    .DB_in(wram_db_out), .DB_out(apu_db_out), .PHI1_FromCore(core_phi1), .PHI2_FromCore(core_phi2),
    .CLK(XTAL_out));  // open: OUT0, OUT1, OUT2, nIN0, nIN1
  WRAM wram (
    .M2(apu_m2__ext), .Addr(apu_ab), .DB_in(apu_db_out), .R_W(apu_r_w__ext), .nRES(nRES), .DB_out(wram_db_out));
  Mock6502 core (
    .PHI0(apu_phi0__cpu), .RDY(apu_rdy__cpu), .SO(1'b1), .nNMI(apu_nnmi_cpu), .nIRQ(apu_nirq_cpu),
    .nRES(nRES), .DB_in(apu_data_to_cpu), .PHI1(core_phi1), .PHI2(core_phi2), .R_W(core_r_w),
    .Addr(core_addr), .DB_out(core_db_out));  // open: SYNC
  AUXDumper dumper (.PHI1(core_phi1), .AUX({1'b0, apu_aux_b, apu_aux_a}), .Addr(dumper_addr), .Data(dumper_data));
  RAM #(.addrWidth(24), .dataWidth(32), .bus("asynch")) ram_1 (
    .addr(dumper_addr), .data(dumper_data), .sel(1'b1), .ld(1'b0), .clr(1'b0));

  // Notes on the sheet:
  //   N.C.
  //   Load regdump here
  //   Taram-param-pam. Pam! Peep, peep, peep. Pipipipip, pip, pibibip
endmodule

module AUXDumper (
  input  PHI1,
  input  [23:0] AUX,
  output [23:0] Addr,
  output [31:0] Data
);

  wire adder_1_p3, counter_2_q, counter_3_q;
  wire [31:0] aux_a_1_a, aux_b_1_a;

  AUX_A aux_a_1 (.d(AUX[7:0]), .a(aux_a_1_a));
  AUX_B aux_b_1 (.d(AUX[23:8]), .a(aux_b_1_a));
  Counter #(.width(23), .max('h7fffff)) counter_1 (.Q(Addr[23:1]), .clk(PHI1));  // open: load, D, count, carry, clr
  Counter #(.width(1), .max('h1)) counter_2 (.Q(counter_2_q), .clk(PHI1));  // open: load, D, count, carry, clr
  Counter #(.width(1), .max('h1), .trigger("falling")) counter_3 (
    .Q(counter_3_q), .clk(PHI1));  // open: load, D, count, carry, clr
  // Adder adder_1: pin names not known; wires that end beside it: aux_a_1_a, aux_b_1_a, adder_1_p3
  // Divider divider_1: pin names not known; wires that end beside it: adder_1_p3, 32'h40000000, Data
  xnor xnor_1 (Addr[0], counter_2_q, counter_3_q);

  // Notes on the sheet:
  //   a + b
  //   The invention of the org to make the ADDR tick EVERY half cycle.
  //    : 2
  //   normalized samples in range [0.0f; 1.0f]
endmodule

module AUX_A (
  input  [7:0] d,
  output [31:0] a
);

  ROM #(.dataWidth(32)) rom_1 (.addr(d), .data(a), .sel(1'b1));

  // Notes on the sheet:
  //   0...255
endmodule

module AUX_B (
  input  [15:0] d,
  output [31:0] a
);

  ROM #(.addrWidth(15), .dataWidth(32)) rom_1 (.addr(d[14:0]), .data(a), .sel(1'b1));

  // Notes on the sheet:
  //   0...32767
endmodule

module Mock6502 (
  input  PHI0,
  input  RDY,
  input  SO,
  input  nNMI,
  input  nIRQ,
  input  nRES,
  input  [7:0] DB_in,
  output PHI1,
  output PHI2,
  output R_W,
  output SYNC,
  output [15:0] Addr,
  output [7:0] DB_out
);

  not not_1 (PHI1, PHI0);

  assign Addr = {16{1'b0}};
  assign DB_out = {8{1'b0}};
  assign PHI2 = PHI0;
  assign R_W = 1'b1;
  assign SYNC = 1'b0;
endmodule

module WRAM (
  input  M2,
  input  [15:0] Addr,
  input  [7:0] DB_in,
  input  R_W,
  input  nRES,
  output [7:0] DB_out
);

  wire nor_1_out, not_1_out, not_2_out;

  not not_1 (not_1_out, nRES);
  nor nor_1 (nor_1_out, Addr[11], Addr[12], Addr[13], Addr[14], Addr[15]);
  not not_2 (not_2_out, R_W);
  RAM #(.addrWidth(11), .bus("separate")) ram_1 (
    .addr(Addr[10:0]), .din(DB_in), .data(DB_out), .str(not_2_out), .sel(nor_1_out), .clk(M2), .ld(R_W),
    .clr(not_1_out));
endmodule
